// Logisim project cpu.circ as structural Verilog
module CPU (
  input  [31:0] Instruction,
  input  CLK,
  output [31:0] s0,
  output [31:0] s1,
  output [31:0] t0,
  output [31:0] t1,
  output [31:0] a0,
  output [31:0] ra,
  output [31:0] sp,
  output [31:0] PC
);

  // Incrementer incrementer_1: pin names not known
  // PC pc_1: pin names not known; wires that end beside it: CLK
  RegFile regfile_1 (
    .Clk(CLK), .RD(Instruction[11:7]), .RS1(Instruction[19:15]), .RS2(Instruction[24:20]), .s0(s0), .s1(s1),
    .t0(t0), .t1(t1), .a0(a0), .ra(ra), .sp(sp));  // open: R1, R2, WE, W
  ImmGenerator immgenerator_1 ();
  // ALU alu_1: pin names not known
  // memory_main main_1: pin names not known; wires that end beside it: CLK

  // Other names for the same wires on the sheet: fetch_addr[31:0] = PC; INST[31:0] = Instruction;
  //   rd[4:0] = Instruction[11:7]; rs1[4:0] = Instruction[19:15]; rs2[4:0] = Instruction[24:20]

  // Notes on the sheet:
  //   NOTE
  //   Please do not modify/replace/move/change/delete/etc input and output pins
  //   These are debug/test outputs from your circuit
endmodule

module control (
  output [2:0] ImSel
);

  wire Btype, comparator_2_eq, comparator_3_eq, comparator_4_eq, Itype, Jtype, Rtype, Stype, Utype;
  wire [6:0] opcode;

  Comparator #(.width(7)) comparator_1 (.a(opcode), .b(7'b0110011), .eq(Rtype));  // open: gt, lt
  Comparator #(.width(7)) comparator_2 (.a(opcode), .b(7'b0000011), .eq(comparator_2_eq));  // open: gt, lt
  Comparator #(.width(7)) comparator_3 (.a(opcode), .b(7'b0010011), .eq(comparator_3_eq));  // open: gt, lt
  Comparator #(.width(7)) comparator_4 (.a(opcode), .b(7'b1100111), .eq(comparator_4_eq));  // open: gt, lt
  Comparator #(.width(7)) comparator_5 (.a(opcode), .b(7'b0100011), .eq(Stype));  // open: gt, lt
  Comparator #(.width(7)) comparator_6 (.a(opcode), .b(7'b1100011), .eq(Btype));  // open: gt, lt
  Comparator #(.width(7)) comparator_7 (.a(opcode), .b(7'b0110111), .eq(Utype));  // open: gt, lt
  Comparator #(.width(7)) comparator_8 (.a(opcode), .b(7'b1101111), .eq(Jtype));  // open: gt, lt
  or or_1 (Itype, comparator_2_eq, comparator_3_eq, comparator_4_eq);
  Multiplexer #(.select(5), .width(3)) multiplexer_1 (
    .in1(3'b000), .in2(3'b001), .in4(3'b010), .in8(3'b011), .in16(3'b100), .in31(3'b101), .out(ImSel),
    .sel({Jtype, Utype, Btype, Stype, Itype}));  // open: in0, in3, in5, in6, in7, in9, in10, in11, in12, in13, in14, in15, in17, in18, in19, in20, in21, in22, in23, in24, in25, in26, in27, in28, in29, in30, en
endmodule
